// Digital circuit UTS_1_3.dig as structural Verilog
module UTS_1_3 (
  input  X,
  input  Y,
  input  Z,
  output x_2
);

  wire not_1_out, not_2_out, not_3_out, not_4_out, or_1_out, or_2_out, or_3_out;

  not not_1 (not_1_out, X);
  not not_2 (not_2_out, Y);
  not not_3 (not_3_out, Z);
  not not_4 (not_4_out, Z);
  or or_1 (or_1_out, not_1_out, not_2_out, not_3_out);
  or or_2 (or_2_out, Y, not_4_out);
  or or_3 (or_3_out, X, Z);
  and and_1 (x_2, or_1_out, or_2_out, or_3_out);

  // Notes on the sheet:
  //   X' Y' Z' + YZ' + XY
endmodule
